// Logisim project O_TRABALHO_FINALMENTE_MEU_DEUS.circ as structural Verilog: 3 circuits, main circuit CIRCUITO
module CIRCUITO (
  input  A,
  input  B,
  input  IN,
  input  \SUBTRAÇÃO ,
  output SOMA,
  output OUT
);

  wire and_1_out, and_2_out, or_1_out, xor_1_out, xor_2_out;

  or or_1 (or_1_out, B, IN);
  xor xor_1 (xor_1_out, A, B);
  and and_1 (and_1_out, IN, B);
  xor xor_2 (xor_2_out, \SUBTRAÇÃO , A);
  and and_2 (and_2_out, xor_2_out, or_1_out);
  xor xor_3 (SOMA, xor_1_out, IN);
  or or_2 (OUT, and_1_out, and_2_out);
endmodule

module DECODIFICADOR (
  input  A0,
  input  A1,
  input  A2,
  input  A3,
  output A,
  output B,
  output C,
  output D,
  output E,
  output F,
  output G
);

  wire and_1_out, and_2_out, and_3_out, and_4_out, and_5_out, and_6_out, and_7_out, and_8_out, and_9_out,
       and_10_out, and_11_out, and_12_out, and_13_out, and_14_out, and_15_out, and_16_out, and_17_out,
       and_18_out, and_19_out, and_20_out, and_21_out, and_22_out, and_23_out, and_24_out, and_25_out,
       and_26_out, and_27_out, and_28_out, and_29_out, and_30_out, and_31_out, and_32_out, and_33_out,
       and_34_out, and_35_out, and_36_out, and_37_out, and_38_out, and_39_out, and_40_out, and_41_out,
       and_42_out, and_43_out, and_44_out, and_45_out, and_46_out, and_47_out, not_1_out, not_2_out,
       not_3_out, not_4_out, not_5_out, not_6_out, not_7_out, not_8_out, not_9_out, not_10_out, not_11_out,
       not_12_out, not_13_out, not_14_out, not_15_out, not_16_out, not_17_out, not_18_out, not_19_out,
       not_20_out, not_21_out, not_22_out, not_23_out, not_24_out, not_25_out, not_26_out, not_27_out,
       not_28_out, not_29_out, not_30_out, not_31_out, not_32_out, not_33_out, not_34_out, not_35_out,
       not_36_out, not_37_out, not_38_out, not_39_out, not_40_out, not_41_out, not_42_out, not_43_out,
       not_44_out, or_1_out, or_2_out, or_3_out, or_4_out, or_5_out, or_7_out, or_8_out, or_9_out, or_10_out,
       or_11_out, or_12_out, or_13_out, or_14_out, or_15_out, or_16_out, or_17_out, or_20_out, or_21_out,
       or_23_out, or_26_out, or_27_out;

  not not_1 (not_1_out, A0);
  not not_2 (not_2_out, A2);
  not not_3 (not_3_out, A0);
  not not_4 (not_4_out, A2);
  not not_5 (not_5_out, A0);
  not not_6 (not_6_out, A0);
  not not_7 (not_7_out, A1);
  not not_8 (not_8_out, A0);
  not not_9 (not_9_out, A1);
  not not_10 (not_10_out, A3);
  not not_11 (not_11_out, A0);
  not not_12 (not_12_out, A1);
  and and_1 (and_1_out, not_1_out, not_2_out);
  not not_13 (not_13_out, A0);
  and and_2 (and_2_out, not_3_out, not_4_out);
  and and_3 (and_3_out, not_5_out, A3);
  and and_4 (and_4_out, not_6_out, not_7_out);
  not not_14 (not_14_out, A3);
  not not_15 (not_15_out, A1);
  and and_5 (and_5_out, not_15_out, A2);
  not not_16 (not_16_out, A2);
  not not_17 (not_17_out, A2);
  not not_18 (not_18_out, A1);
  and and_6 (and_6_out, not_18_out, not_19_out);
  not not_19 (not_19_out, A3);
  and and_7 (and_7_out, A2, not_20_out);
  not not_20 (not_20_out, A3);
  and and_8 (and_8_out, A0, A2);
  and and_9 (and_9_out, A0, A1);
  not not_21 (not_21_out, A2);
  not not_22 (not_22_out, A3);
  and and_10 (and_10_out, not_8_out, A1);
  not not_23 (not_23_out, A2);
  and and_11 (and_11_out, not_9_out, A2);
  and and_12 (and_12_out, A2, not_10_out);
  and and_13 (and_13_out, not_11_out, A1);
  not not_24 (not_24_out, A2);
  not not_25 (not_25_out, A1);
  not not_26 (not_26_out, A1);
  not not_27 (not_27_out, A3);
  not not_28 (not_28_out, A0);
  not not_29 (not_29_out, A0);
  and and_14 (and_14_out, A0, not_12_out);
  not not_30 (not_30_out, A2);
  not not_31 (not_31_out, A0);
  not not_32 (not_32_out, A1);
  not not_33 (not_33_out, A3);
  not not_34 (not_34_out, A1);
  not not_35 (not_35_out, A3);
  and and_15 (and_15_out, not_13_out, A2);
  and and_16 (and_16_out, A0, not_36_out);
  not not_36 (not_36_out, A2);
  not not_37 (not_37_out, A2);
  not not_38 (not_38_out, A0);
  not not_39 (not_39_out, A1);
  and and_17 (and_17_out, and_4_out, not_14_out);
  and and_18 (and_18_out, and_5_out, A3);
  and and_19 (and_19_out, A1, not_16_out);
  and and_20 (and_20_out, A1, A2);
  not not_40 (not_40_out, A3);
  and and_21 (and_21_out, A0, not_17_out);
  not not_41 (not_41_out, A3);
  or or_1 (or_1_out, and_6_out, and_7_out);
  or or_2 (or_2_out, and_8_out, and_9_out);
  and and_22 (and_22_out, not_21_out, not_22_out);
  and and_23 (and_23_out, and_10_out, not_23_out);
  or or_3 (or_3_out, and_11_out, and_12_out);
  and and_24 (and_24_out, and_13_out, not_24_out);
  and and_25 (and_25_out, A0, not_25_out);
  and and_26 (and_26_out, A0, A3);
  and and_27 (and_27_out, not_26_out, not_27_out);
  and and_28 (and_28_out, not_28_out, A2);
  and and_29 (and_29_out, not_29_out, A1);
  and and_30 (and_30_out, A1, A2);
  and and_31 (and_31_out, and_14_out, not_30_out);
  not not_42 (not_42_out, A3);
  and and_32 (and_32_out, not_31_out, not_32_out);
  and and_33 (and_33_out, and_1_out, not_33_out);
  and and_34 (and_34_out, not_34_out, not_35_out);
  and and_35 (and_35_out, and_15_out, A3);
  and and_36 (and_36_out, and_16_out, A3);
  or or_4 (or_4_out, and_2_out, and_3_out);
  and and_37 (and_37_out, not_37_out, A3);
  and and_38 (and_38_out, not_38_out, A1);
  and and_39 (and_39_out, A0, not_39_out);
  or or_5 (or_5_out, and_17_out, and_18_out);
  and and_40 (and_40_out, and_19_out, A3);
  and and_41 (and_41_out, and_20_out, not_40_out);
  and and_42 (and_42_out, and_21_out, not_41_out);
  or or_6 (E, or_1_out, or_2_out);
  not not_43 (not_43_out, A3);
  not not_44 (not_44_out, A1);
  or or_7 (or_7_out, or_3_out, and_24_out);
  or or_8 (or_8_out, and_25_out, and_26_out);
  or or_9 (or_9_out, and_27_out, and_28_out);
  or or_10 (or_10_out, or_9_out, and_43_out);
  and and_43 (and_43_out, and_29_out, A3);
  or or_11 (or_11_out, and_30_out, and_31_out);
  and and_44 (and_44_out, A0, not_42_out);
  or or_12 (or_12_out, and_32_out, and_33_out);
  or or_13 (or_13_out, or_4_out, and_37_out);
  or or_14 (or_14_out, and_38_out, and_39_out);
  or or_15 (or_15_out, or_5_out, and_40_out);
  or or_16 (or_16_out, and_41_out, and_42_out);
  or or_17 (or_17_out, and_22_out, and_23_out);
  and and_45 (and_45_out, A1, not_43_out);
  and and_46 (and_46_out, A0, not_44_out);
  and and_47 (and_47_out, A0, A2);
  or or_18 (G, or_7_out, or_8_out);
  or or_19 (A, or_10_out, or_20_out);
  or or_20 (or_20_out, or_11_out, and_44_out);
  or or_21 (or_21_out, or_12_out, and_34_out);
  or or_22 (B, or_21_out, or_23_out);
  or or_23 (or_23_out, and_35_out, and_36_out);
  or or_24 (C, or_13_out, or_14_out);
  or or_25 (D, or_15_out, or_16_out);
  or or_26 (or_26_out, or_17_out, and_45_out);
  or or_27 (or_27_out, and_46_out, and_47_out);
  or or_28 (F, or_26_out, or_27_out);
endmodule

module CENTRAL (
  input  SUBTRADOR,
  input  A0,
  input  A1,
  input  A2,
  input  A3,
  input  in_6,
  input  B3,
  input  B2,
  input  B1,
  input  B0
);

  wire circuito_1_soma, circuito_2_out, circuito_2_soma, circuito_3_out, circuito_3_soma, circuito_4_out,
       circuito_4_soma, decodificador_1_a, decodificador_1_b, decodificador_1_c, decodificador_1_d,
       decodificador_1_e, decodificador_1_f, decodificador_1_g;

  CIRCUITO circuito_1 (
    .A(A3), .B(B3), .IN(circuito_2_out), .\SUBTRAÇÃO (SUBTRADOR), .SOMA(circuito_1_soma));  // open: OUT
  CIRCUITO circuito_2 (
    .A(A2), .B(B2), .IN(circuito_3_out), .\SUBTRAÇÃO (SUBTRADOR), .SOMA(circuito_2_soma), .OUT(circuito_2_out));
  CIRCUITO circuito_3 (
    .A(A1), .B(B1), .IN(circuito_4_out), .\SUBTRAÇÃO (SUBTRADOR), .SOMA(circuito_3_soma), .OUT(circuito_3_out));
  CIRCUITO circuito_4 (
    .A(A0), .B(B0), .IN(in_6), .\SUBTRAÇÃO (SUBTRADOR), .SOMA(circuito_4_soma), .OUT(circuito_4_out));
  DECODIFICADOR decodificador_1 (
    .A0(circuito_1_soma), .A1(circuito_2_soma), .A2(circuito_3_soma), .A3(circuito_4_soma),
    .A(decodificador_1_a), .B(decodificador_1_b), .C(decodificador_1_c), .D(decodificador_1_d),
    .E(decodificador_1_e), .F(decodificador_1_f), .G(decodificador_1_g));
  _7_Segment_Display u_7_segment_display_1 (
    .g(decodificador_1_g), .f(decodificador_1_f), .a(decodificador_1_a), .b(decodificador_1_b),
    .e(decodificador_1_e), .d(decodificador_1_d), .c(decodificador_1_c));  // open: dp
endmodule
