// Logisim project lucio2.circ as structural Verilog: 2 circuits, main circuit main
module main (
  input  in_1
);

  wire and_1_out, and_2_out, clock_1_out, not_1_out;
  wire [3:0] adder_1_out, counter_1_q, multiplexer_1_out, multiplexer_2_out, register_1_q, register_2_q;
  wire [7:0] rom_1_data;

  Clock clock_1 (.out(clock_1_out));
  Counter #(.width(4), .max('hf)) counter_1 (
    .Q(counter_1_q), .clk(clock_1_out), .clr(in_1));  // open: load, D, count, carry
  not not_1 (not_1_out, clock_1_out);
  ROM #(.addrWidth(4)) rom_1 (.addr(counter_1_q), .data(rom_1_data));  // open: sel
  LED led_1 (.in(register_1_q[3]));
  LED led_2 (.in(register_1_q[2]));
  LED led_3 (.in(register_1_q[1]));
  LED led_4 (.in(register_1_q[0]));
  and and_1 (and_1_out, clock_1_out, rom_1_data[4]);
  LED led_5 (.in(register_2_q[3]));
  and and_2 (and_2_out, rom_1_data[5], not_1_out);
  LED led_6 (.in(register_2_q[2]));
  LED led_7 (.in(register_2_q[1]));
  LED led_8 (.in(register_2_q[0]));
  Register #(.width(4)) register_1 (.D(adder_1_out), .Q(register_1_q), .clk(and_2_out));  // open: en, clr
  Register #(.width(4)) register_2 (.D(adder_1_out), .Q(register_2_q), .clk(and_1_out));  // open: en, clr
  Multiplexer #(.width(4)) multiplexer_1 (
    .in0(rom_1_data[3:0]), .in1(register_1_q), .out(multiplexer_1_out), .sel(rom_1_data[6]));  // open: en
  Multiplexer #(.width(4)) multiplexer_2 (
    .in0(4'b0000), .in1(register_2_q), .out(multiplexer_2_out), .sel(rom_1_data[7]));  // open: en
  Adder #(.width(4)) adder_1 (
    .a(multiplexer_1_out), .b(multiplexer_2_out), .out(adder_1_out), .cin(1'b0));  // open: cout
  Hex_Digit_Display hex_digit_display_1 (.value(adder_1_out));  // open: dp

  // Notes on the sheet:
  //   7672
  //   a*d-b+c
  //   contents of rom_1 (hex, n*v repeats v):
  //   17 27 e0 0 e 1a e2 0 18 17 e1
endmodule

module d (
  input  in_1,
  input  in_2,
  input  in_3,
  input  in_4,
  input  in_5,
  input  in_6,
  input  in_7,
  input  in_8
);

  wire and_1_out, and_2_out, clock_1_out;
  wire [3:0] adder_1_out, multiplexer_1_out, multiplexer_2_out, register_1_q, register_2_q;

  Clock clock_1 (.out(clock_1_out));
  ROM rom_1 ();  // open: addr, data, sel
  LED led_1 (.in(register_1_q[2]));
  LED led_2 (.in(register_1_q[1]));
  LED led_3 (.in(register_1_q[3]));
  LED led_4 (.in(register_1_q[0]));
  and and_1 (and_1_out, clock_1_out, in_3);
  and and_2 (and_2_out, clock_1_out, in_4);
  LED led_5 (.in(register_2_q[3]));
  LED led_6 (.in(register_2_q[2]));
  LED led_7 (.in(register_2_q[1]));
  LED led_8 (.in(register_2_q[0]));
  Register #(.width(4)) register_1 (.D(adder_1_out), .Q(register_1_q), .clk(and_1_out));  // open: en, clr
  Register #(.width(4)) register_2 (.D(adder_1_out), .Q(register_2_q), .clk(and_2_out));  // open: en, clr
  Multiplexer #(.width(4)) multiplexer_1 (
    .in0(4'b0000), .in1(register_2_q), .out(multiplexer_1_out), .sel(in_1));  // open: en
  Multiplexer #(.width(4)) multiplexer_2 (
    .in0({in_5, in_6, in_7, in_8}), .in1(register_1_q), .out(multiplexer_2_out), .sel(in_2));  // open: en
  Adder #(.width(4)) adder_1 (
    .a(multiplexer_2_out), .b(multiplexer_1_out), .out(adder_1_out), .cin(1'b0));  // open: cout
  Hex_Digit_Display hex_digit_display_1 (.value(adder_1_out));  // open: dp
endmodule
